// Logisim project AU (1).circ as structural Verilog: 1 circuit, main circuit main
module main (
  input  [3:0] in_1,
  input  [3:0] in_2,
  input  [3:0] in_3,
  output out_4,
  output out_5,
  output out_6,
  output out_7,
  output out_8
);

  wire main_1_p7, main_2_p7, main_3_p7, main_4_p7, main_5_p5, main_6_p5, main_7_p5, not_1_out, not_2_out,
       not_3_out, not_4_out, not_5_out;

  not not_1 (not_1_out, in_2[0]);
  not not_2 (not_2_out, in_2[2]);
  not not_3 (not_3_out, in_3[0]);
  not not_4 (not_4_out, in_3[2]);
  not not_5 (not_5_out, in_3[3]);
  // _4x1_mux_main main_1: pin names not known; wires that end beside it: in_2[0], not_1_out, in_3[3], not_5_out, in_1[1], in_1[2], main_1_p7
  // _4x1_mux_main main_2: pin names not known; wires that end beside it: in_2[2], not_2_out, in_3[3], not_5_out, in_1[1], in_1[2], main_2_p7
  // _4x1_mux_main main_3: pin names not known; wires that end beside it: in_3[0], not_3_out, in_3[3], not_5_out, in_1[1], in_1[2], main_3_p7
  // _4x1_mux_main main_4: pin names not known; wires that end beside it: in_3[2], not_4_out, in_3[3], not_5_out, in_1[1], in_1[2], main_4_p7
  // full_adder_main main_5: pin names not known; wires that end beside it: in_1[3], main_1_p7, in_1[0], out_4, main_5_p5
  // full_adder_main main_6: pin names not known; wires that end beside it: in_2[1], main_2_p7, main_5_p5, out_5, main_6_p5
  // full_adder_main main_7: pin names not known; wires that end beside it: in_2[3], main_3_p7, main_6_p5, out_6, main_7_p5
  // full_adder_main main_8: pin names not known; wires that end beside it: in_3[1], main_4_p7, main_7_p5, out_7, out_8
endmodule
